// Logisim project Priority_Encoder.circ as structural Verilog: 1 circuit, main circuit main
module main (
  input  in_1,
  input  in_2,
  input  in_3,
  output out_4,
  output out_5,
  output out_6
);

  wire not_1_out;

  not not_1 (not_1_out, in_1);
  and and_1 (out_5, not_1_out, in_2);
  or or_1 (out_6, in_1, in_2, in_3);

  assign out_4 = in_1;
endmodule
